# Fritzing sketch wemos_d1_mini_custom_board (saved by Fritzing 0.9.6b)

parts:
  WeMos_D1_Mini1 = WeMos D1 Mini
  R1 = Resistor [tolerance=±5% power=0.25 resistance=10k package=THT]  # not connected
  LED1 = LED - 5mm [color="Green (570nm)" current=0.030 package="5 mm [THT]"]
  S2 = Pushbutton [package="[THT]"]
  S3 = Pushbutton [package="[THT]"]
  S4 = Pushbutton [package="[THT]"]
  WeMos_D1_Mini_Battery_Shield1 = WeMos D1 Mini Battery Shield
  S1 = Toggle Switch [package=THT]
  R2 = Resistor [tolerance=±5% power=0.25 resistance=10k package=THT]  # not connected
  R3 = Resistor [tolerance=±5% power=0.25 resistance=10k package=THT]
  OLED1 = OLED 128x64 I2C Monochrome Display

nets:
  N1: WeMos_D1_Mini1.5V, S1.L2
  N2: WeMos_D1_Mini1.D1, OLED1.SCK
  N3: WeMos_D1_Mini1.D2, OLED1.SDA
  N4: WeMos_D1_Mini1.D5, S4.Pin_3, S4.Pin_4
  N5: WeMos_D1_Mini1.D6, S3.Pin_3
  N6: WeMos_D1_Mini1.D7, S2.Pin_2
  N7: WeMos_D1_Mini1.D8, LED1.anode
  N8: WeMos_D1_Mini1.G, S2.Pin_3, S2.Pin_4, S3.Pin_1, S3.Pin_2, S4.Pin_1, WeMos_D1_Mini_Battery_Shield1.G
  N9: LED1.cathode, OLED1.GND
  N10: WeMos_D1_Mini_Battery_Shield1.5V, S1.COM
  N11: R3.Pin_0, OLED1.VDD
